# Fritzing sketch heart_project (saved by Fritzing 1.0.4)
breadboards: 2

parts:
  U1 = LCD-16X2 [package=lcd-16x2]
  R2 = Resistor [tolerance=±5% power=0.25W resistance=220 package=THT]
  Mod1 = Raspberry Pi Pico W
  R3 = Rotary Potentiometer (Small) [maximum_resistance=10kΩ knob_status=50% power=0.5W package=THT]
  S1 = Pushbutton [package="[THT]"]
  S2 = Pushbutton [package="[THT]"]
  S3 = Pushbutton [package="[THT]"]
  S4 = Pushbutton [package="[THT]"]

nets:
  N1: U1.VSS, U1.R_W, U1.K, Mod1.pin_3, Mod1.pin_8, Mod1.pin_13, Mod1.pin_18, Mod1.pin_23, Mod1.pin_28, Mod1.pin_33, Mod1.pin_38, R3.leg1, R3.leg2
  N2: U1.VDD, R2.Pin_1, Mod1.pin_40
  N3: U1.VO, R3.wiper
  N4: U1.RS, Mod1.pin_21
  N5: U1.E, Mod1.pin_20
  N6: U1.DB4, Mod1.pin_10
  N7: U1.DB5, Mod1.pin_9
  N8: U1.DB6, Mod1.pin_7
  N9: U1.DB7, Mod1.pin_6
  N10: U1.A, R2.Pin_0
  N11: Mod1.pin_15, S4.Pin_1, S4.Pin_2
  N12: Mod1.pin_16, S3.Pin_1, S3.Pin_2
  N13: Mod1.pin_17, S2.Pin_1, S2.Pin_2
  N14: Mod1.pin_19, S1.Pin_1, S1.Pin_2
  N15: S1.Pin_3, S1.Pin_4, S2.Pin_3, S2.Pin_4, S3.Pin_3, S3.Pin_4, S4.Pin_3, S4.Pin_4

custom parts:
  Raspberry Pi Pico W: Raspberry Pi Pico W. Based around the RP2040 microcontroller the Pico W is a low cost microcontroller device bringing Raspberry Pi quality, cost, and easy of use to the microcontroller space. The areas marked KEEPOUT in pcb silkscreen should not have traces running through them to avoid shorts on a soldered in module!
